# Fritzing sketch BuzzerFirmata (saved by Fritzing 0.9.1b)

parts:
  J1 = Piezo Speaker
  Part1 = Arduino Uno (Rev3)

nets:
  N1: J1.pin1, Part1.GND
  N2: J1.pin2, Part1.D7

notes:
  Any pin can be used for the positive pin of the buzzer as it is specified from within S4A.
