# Fritzing sketch LCDFirmata (saved by Fritzing 0.9.1b)
breadboards: 1

parts:
  Part1 = Arduino Uno (Rev3)
  U1 = POT [package=pot_alpha_rv16af-20]
  LCD_I2C1 = LCD screen
  R1 = Resistor [tolerance=±5% resistance=220 package="1206 [SMD]"]

nets:
  N1: Part1.D11_PWM/MOSI, LCD_I2C1.E
  N2: Part1.D12/MISO, LCD_I2C1.RS
  N3: Part1.D2, LCD_I2C1.DB7
  N4: Part1.D3_PWM, LCD_I2C1.DB6
  N5: Part1.D4, LCD_I2C1.DB5
  N6: Part1.D5_PWM, LCD_I2C1.DB4
  5V: Part1.5V, U1.E, LCD_I2C1.VDD, R1.Pin_0
  GND: Part1.GND, U1.A, LCD_I2C1.VSS, LCD_I2C1.R/W, LCD_I2C1.LED-
  N7: U1.S, LCD_I2C1.V0
  N8: LCD_I2C1.LED+, R1.Pin_1
