# Fritzing sketch Ultrasound_HC_SR04Firmata (saved by Fritzing 0.9.1b)
breadboards: 1

parts:
  Part1 = Arduino Uno (Rev3) - ICSP
  Part2 = HC-SR04 Ultrasonic Rangemeter

nets:
  N1: Part1.D8, Part2.Echo
  N2: Part1.D9_PWM, Part2.Trig
  5V: Part1.5V, Part2.VCC
  GND: Part1.GND, Part2.GND

notes:
  Must use pins 8 and 9 as shown
